# Fritzing sketch Wiring (saved by Fritzing 1.0.3b)
circuit board: 11.523cm x 5.91384cm
breadboards: 1

parts:
  Bauteil1 = Arduino Nano (Rev3.0)
  J2 = Piezo Speaker
  Bauteil2 = HX711 Weighing Sensor Module
  LCD1 = 1_7in tft lcd
  RE1 = KY-040 Rotary encoder [package="Breakout board"]
  S1 = Round Pushbutton
  S2 = Round Pushbutton
  S3 = Toggle Switch [package=THT]  # not connected
  S4 = Toggle Switch [package=THT]
  Power_plug1 = Power plug
  J1 = Basic Servo
  Bauteil3 = I2C level shifter bidirectional

nets:
  GND: Bauteil1.GND, J2.pin1, Bauteil2.GND, LCD1.pin_1, LCD1.pin_14, RE1.GND, S1.leg0, S2.leg0, S4.COM, Power_plug1.GND, J1.gnd, Bauteil3.GND
  N1: Bauteil1.D2, RE1.CLK
  N2: Bauteil1.D3, RE1.DT
  N3: Bauteil1.D4, RE1.SW
  N4: Bauteil1.D5, J1.pulse
  N5: Bauteil1.D6, J2.pin2
  N6: Bauteil1.D8, LCD1.pin_5
  N7: Bauteil1.D9, Bauteil3.HV3
  N8: Bauteil1.D10, Bauteil3.HV4
  N9: Bauteil1.D11/MOSI, Bauteil3.HV2
  VCC: Bauteil1.VIN, Bauteil2.VCC, LCD1.pin2, RE1.Vcc, Power_plug1.VCC, J1.vcc, Bauteil3.HV
  N10: Bauteil1.A5, Bauteil2.CK/TX
  N11: Bauteil1.A4, Bauteil2.DO/RX
  N12: Bauteil1.A3, S4.L1
  N13: Bauteil1.A2, S4.L2
  N14: Bauteil1.A1, S2.leg1
  N15: Bauteil1.A0, S1.leg1
  N16: Bauteil1.3V3, LCD1.pin_8, Bauteil3.LV
  N17: Bauteil1.D13/SCK, Bauteil3.HV1
  N18: LCD1.pin3, Bauteil3.LV1
  N19: LCD1.pin4, Bauteil3.LV2
  N20: LCD1.pin_6, Bauteil3.LV3
  N21: LCD1.pin_7, Bauteil3.LV4

custom parts:
  1_7in tft lcd: This is the Zoll 1.77in spi lcd display. The 1.77" display has 128x160 color pixels.
  KY-040 Rotary encoder: KY-040 Rotary Encoder with switch on breakout borad from AZ Delivery
